# Fritzing sketch nodoLed (1) (saved by Fritzing 0.9.6b)

parts:
  Q1 = NPN-Transistor [package="TO92 [THT]"]
  Q2 = NPN-Transistor [package="TO92 [THT]"]
  Q3 = NPN-Transistor [package="TO92 [THT]"]
  R1 = Resistor [tolerance=±5% resistance=1k package="2512 [SMD]"]
  R2 = Resistor [tolerance=±5% resistance=1k package="2512 [SMD]"]
  R3 = Resistor [tolerance=±5% resistance=1k package="2512 [SMD]"]
  WeMos_D1_Mini1 = WeMos D1 Mini
  HLK-PM1 = HLK-PM01
  HLK-PM2 = HLK-PM12 [part_number=HLK-PM12]
  Componente1 = LilyPad Tri-Color LED

nets:
  N1: Q1.E, Q2.E, Q3.E, WeMos_D1_Mini1.G, HLK-PM1.-Vo, HLK-PM2.-Vo
  N2: Q1.B, R1.Pin_1
  N3: Q1.C, Componente1.R
  N4: Q2.B, R2.Pin_1
  N5: Q2.C, Componente1.B
  N6: Q3.B, R3.Pin_1
  N7: Q3.C, Componente1.G
  N8: R1.Pin_0, WeMos_D1_Mini1.D7
  N9: R2.Pin_0, WeMos_D1_Mini1.D6
  N10: R3.Pin_0, WeMos_D1_Mini1.D5
  N11: WeMos_D1_Mini1.5V, HLK-PM1.+Vo
  N12: HLK-PM2.+Vo, Componente1.+
